# Fritzing sketch clock_box_schematic_V2.4.0 (saved by Fritzing 0.9.3b)
breadboards: 1

parts:
  DYN_SYNC_POT = Rotary Potentiometer (Large) [maximum_resistance=10kΩ package=THT]
  MIDI_1_POT = Rotary Potentiometer (Large) [maximum_resistance=10kΩ package=THT]
  MIDI_2_POT = Rotary Potentiometer (Large) [maximum_resistance=10kΩ package=THT]
  MIDI_3_POT = Rotary Potentiometer (Large) [maximum_resistance=10kΩ package=THT]
  MIDI_4_POT = Rotary Potentiometer (Large) [maximum_resistance=10kΩ package=THT]
  BPM_POT = Rotary Potentiometer (Large) [maximum_resistance=10kΩ package=THT]
  DIN_SYNC = DIN-5 jack (MIDI) [package=THT]
  MIDI_OUT_1 = DIN-5 jack (MIDI) [package=THT]
  MIDI_OUT_2 = DIN-5 jack (MIDI) [package=THT]
  MIDI_OUT_3 = DIN-5 jack (MIDI) [package=THT]
  MIDI_OUT_4 = DIN-5 jack (MIDI) [package=THT]
  R2 = Resistor [tolerance=±5% resistance=47 package="0603 [SMD]"]
  R3 = Resistor [tolerance=±5% resistance=47 package="0603 [SMD]"]
  R4 = Resistor [tolerance=±5% resistance=47 package="0603 [SMD]"]
  R5 = Resistor [tolerance=±5% resistance=47 package="0603 [SMD]"]
  BPM_TEMPO_LED = LED - 5mm [color="Red (633nm)" package="5 mm [THT]"]
  START_STOP_BUTTON = Round Pushbutton
  R6 = Resistor [tolerance=±5% resistance=10k package="0603 [SMD]"]
  R7 = Resistor [tolerance=±5% resistance=100 package="2512 [SMD]"]
  SAVE_BUTTON = Round Pushbutton
  R8 = Resistor [tolerance=±5% resistance=10k package="0603 [SMD]"]
  Part5 = TFT 2.2 inch 320x240 w microSD [part_number=1480]
  Teensy_3_2 = Teensy 3.0

nets:
  N1: DYN_SYNC_POT.leg1, MIDI_1_POT.leg1, MIDI_2_POT.leg1, MIDI_3_POT.leg1, MIDI_4_POT.leg1, BPM_POT.leg1, MIDI_OUT_1.4, MIDI_OUT_2.4, MIDI_OUT_3.4, MIDI_OUT_4.4, Part5.VIN, Part5.BACKLIGHT
  N2: DYN_SYNC_POT.wiper, Teensy_3_2.A5/D19
  N3: DYN_SYNC_POT.leg2, MIDI_1_POT.leg2, MIDI_2_POT.leg2, MIDI_3_POT.leg2, MIDI_4_POT.leg2, BPM_POT.leg2, MIDI_OUT_4.2, START_STOP_BUTTON.leg1, R6.Pin_0, R7.Pin_1
  N4: MIDI_1_POT.wiper, Teensy_3_2.A8/D22
  N5: MIDI_2_POT.wiper, Teensy_3_2.A9/D23
  N6: MIDI_3_POT.wiper, Teensy_3_2.A12
  N7: MIDI_4_POT.wiper, Teensy_3_2.A13
  N8: BPM_POT.wiper, Teensy_3_2.A4/D18
  N9: DIN_SYNC.3, Teensy_3_2.D24
  N10: DIN_SYNC.2, Teensy_3_2.D33
  N11: DIN_SYNC.1, Teensy_3_2.D31
  N12: MIDI_OUT_1.5, R2.Pin_1
  N13: MIDI_OUT_1.2, MIDI_OUT_2.2, MIDI_OUT_3.2
  N14: MIDI_OUT_2.5, R3.Pin_1
  N15: MIDI_OUT_3.5, R4.Pin_1
  N16: MIDI_OUT_4.5, R5.Pin_1
  N17: R2.Pin_0, Teensy_3_2.D1
  N18: R3.Pin_0, Teensy_3_2.D8
  N19: R4.Pin_0, Teensy_3_2.A0/D14
  N20: R5.Pin_0, Teensy_3_2.A1/D15
  N21: BPM_TEMPO_LED.cathode, Teensy_3_2.D5
  N22: BPM_TEMPO_LED.anode, R7.Pin_0
  N23: START_STOP_BUTTON.leg0, R6.Pin_1, Teensy_3_2.D2
  N24: SAVE_BUTTON.leg0, Teensy_3_2.D6
  N25: SAVE_BUTTON.leg1, R8.Pin_0
  N26: R8.Pin_1, Teensy_3_2.GND
  N27: Part5.DC, Teensy_3_2.D9
  N28: Part5.RESET, Teensy_3_2.D3
  N29: Part5.SDCS, Teensy_3_2.D4
  N30: Part5.LCDCS, Teensy_3_2.D10
  N31: Part5.MOSI, Teensy_3_2.D11
  N32: Part5.MISO, Teensy_3_2.D12
  N33: Part5.SCLK, Teensy_3_2.D13

custom parts:
  TFT 2.2 inch 320x240 w microSD: This lovely little display breakout is the best way to add a small, colorful and bright display to any project. Since the display uses 4-wire SPI to communicate and has its own pixel-addressable frame buffer, it can be used with every kind of microcontroller. Even a very small one with low memory and few pins available! The 2.2" display has 320x240 color pixels.
